# Fritzing sketch i2c-tester-sample-connection (saved by Fritzing 0.9.4)
breadboards: 1

parts:
  J1 = female pin header, 4 pins [form="♀ (female)"]
  IC1 = 24LC01 [package=THT]

nets:
  N1: J1.pin1, IC1.+V
  N2: J1.pin2, IC1.SCL_-_I2C_Clock
  N3: J1.pin3, IC1.SDA_-_I2C_Data
  N4: J1.pin4, IC1.A0, IC1.A1, IC1.A2, IC1.0V

notes:
  VCC
  SCL
  SDA
  GND
  I2C Test Terminal Socket
